# Fritzing sketch Internet Radio (saved by Fritzing 1.0.0rc)
circuit board: 8.64163cm x 7.92981cm
breadboards: 2

parts:
  OLED1 = OLED 128x64 I2C Monochrome Display
  U1 = ESP32-WROOM-32D-NodeMCU
  RE1 = KY-040 Rotary encoder [package=THT]
  S1 = Pushbutton [package="[THT]"]
  S2 = Pushbutton [package="[THT]"]
  R1 = Resistor [tolerance=±5% power=0.25W resistance=10k package=THT]
  R2 = Resistor [tolerance=±5% power=0.25W resistance=10k package=THT]
  A1 = VS1003/1053 MP3 module

nets:
  GND: OLED1.GND, U1.GND#50, RE1.GND, R1.Pin_1, R2.Pin_1, A1.Pin_8
  VDD: OLED1.VDD, U1.3.3V, S1.Pin_1, S1.Pin_2, R1.Pin_0
  N1: OLED1.SCK, U1.G22
  N2: OLED1.SDA, U1.G19, U1.GND#44, U1.G21, U1.TXD, A1.Pin_6
  N3: U1.EN, A1.Pin_7
  N4: U1.G34, S1.Pin_3, S1.Pin_4
  N5: U1.G35, U1.G13, U1.CLK, A1.Pin_3
  N6: U1.G32, U1.GND#13, U1.SD3, U1.SD0, A1.Pin_2
  N7: U1.G33, A1.Pin_1
  N8: U1.G25, S2.Pin_3, S2.Pin_4
  N9: U1.G26, RE1.SW
  N10: U1.5V, A1.Pin_9
  N11: U1.G16, RE1.DT
  N12: U1.G17, RE1.CLK
  N13: U1.G18, A1.Pin_4
  N14: U1.G23, A1.Pin_5
  N15: S2.Pin_1, S2.Pin_2, R2.Pin_0

custom parts:
  KY-040 Rotary encoder: KY-040 Rotary Encoder with switch on breakout borad from AZ Delivery
  VS1003/1053 MP3 module: VS1003/1053 MP3 module.
